# Fritzing sketch WiFi_Device_Sketch (saved by Fritzing 1.0.1rc)

parts:
  M1 = Humidity and Temperature Sensor DHT11
  DHT1 = DHT22 Humidity and Temperature Sensor
  DS1 = DS18B20 1-Wire Temperature Sensor Probe
  J1 = Basic Servo  # not connected
  IC1 = DIP - 6 pins [chip_label="5V RELAY" package="DIP (Dual Inline) [THT]"]
  IC4 = DIP - 6 pins [chip_label="5V RELAY" package="DIP (Dual Inline) [THT]"]
  IC3 = DIP - 6 pins [chip_label="5V RELAY" package="DIP (Dual Inline) [THT]"]
  IC2 = DIP - 6 pins [chip_label="5V RELAY" package="DIP (Dual Inline) [THT]"]
  R2 = Resistor [tolerance=±5% resistance=10k package="2010 [SMD]"]
  R3 = Resistor [tolerance=±5% resistance=10k package="2010 [SMD]"]

nets:
  VDD: M1.Vcc, DHT1.VDD, DS1.VDD, R3.Pin_0
  N1: M1.Data, R2.Pin_1
  GND: M1.GND, DHT1.GND, DS1.GND
  N2: DHT1.DATA, R3.Pin_1
  N3: IC1.DC+, IC4.DC+, IC3.DC+, IC2.DC+
  N4: IC1.DC-, IC4.DC-, IC3.DC-, IC2.DC-

custom parts:
  Humidity and Temperature Sensor DHT11: Digital relative humidity & temperature sensor DHT11
  DIP - 6 pins: A DIP stand-in part for whatever IC you want. With 6 pins on a 300mil dual inline package (DIP) footprint.
